// Logisim project 1607048.circ as structural Verilog: 3 circuits, main circuit main
module main (
  input  S1,
  input  S0,
  input  Cin,
  input  A0,
  input  B0,
  input  A1,
  input  B1,
  input  A2,
  input  B2,
  input  A3,
  input  B3,
  input  A4,
  input  B4,
  input  A5,
  input  B5,
  input  A6,
  input  B6,
  input  A7,
  input  B7,
  output F0,
  output F1,
  output F2,
  output F3,
  output F4,
  output F5,
  output F6,
  output F7
);

  wire fa_1_c, fa_2_c, fa_3_c, fa_4_c, fa_5_c, fa_6_c, fa_7_c, fa_8_c, tc_oz_1_y, tc_oz_2_y, tc_oz_3_y,
       tc_oz_4_y, tc_oz_5_y, tc_oz_6_y, tc_oz_7_y, tc_oz_8_y;

  TC_OZ tc_oz_1 (.B(B0), .S0(S0), .S(S1), .Y(tc_oz_1_y));
  TC_OZ tc_oz_2 (.B(B1), .S0(S0), .S(S1), .Y(tc_oz_2_y));
  TC_OZ tc_oz_3 (.B(B2), .S0(S0), .S(S1), .Y(tc_oz_3_y));
  TC_OZ tc_oz_4 (.B(B3), .S0(S0), .S(S1), .Y(tc_oz_4_y));
  TC_OZ tc_oz_5 (.B(B4), .S0(S0), .S(S1), .Y(tc_oz_5_y));
  TC_OZ tc_oz_6 (.B(B5), .S0(S0), .S(S1), .Y(tc_oz_6_y));
  TC_OZ tc_oz_7 (.B(B6), .S0(S0), .S(S1), .Y(tc_oz_7_y));
  TC_OZ tc_oz_8 (.B(B7), .S0(S0), .S(S1), .Y(tc_oz_8_y));
  FA fa_1 (.X(A0), .Y(Cin), .Z(tc_oz_1_y), .S(F0), .C(fa_1_c));
  FA fa_2 (.X(A1), .Y(fa_1_c), .Z(tc_oz_2_y), .S(F1), .C(fa_2_c));
  FA fa_3 (.X(A2), .Y(fa_2_c), .Z(tc_oz_3_y), .S(F2), .C(fa_3_c));
  FA fa_4 (.X(A3), .Y(fa_3_c), .Z(tc_oz_4_y), .S(F3), .C(fa_4_c));
  FA fa_5 (.X(A4), .Y(fa_4_c), .Z(tc_oz_5_y), .S(F4), .C(fa_5_c));
  FA fa_6 (.X(A5), .Y(fa_5_c), .Z(tc_oz_6_y), .S(F5), .C(fa_6_c));
  FA fa_7 (.X(A6), .Y(fa_6_c), .Z(tc_oz_7_y), .S(F6), .C(fa_7_c));
  FA fa_8 (.X(A7), .Y(fa_7_c), .Z(tc_oz_8_y), .S(F7), .C(fa_8_c));
  LED Cout (.in(fa_8_c));

  // Notes on the sheet:
  //   Roll: 1607048
  //   A=4 (00000100)
  //   B=8 (00001000)
endmodule

module FA (
  input  X,
  input  Y,
  input  Z,
  output S,
  output C
);

  wire AND_1_out, AND_2_out, XOR_1_out;

  xor XOR_1 (XOR_1_out, X, Y);
  and AND_1 (AND_1_out, X, Y);
  xor XOR_2 (S, XOR_1_out, Z);
  and AND_2 (AND_2_out, Z, XOR_1_out);
  or OR (C, AND_2_out, AND_1_out);

  // Notes on the sheet:
  //   Roll: 1607048
endmodule

// TC
module TC_OZ (
  input  B,
  input  S0,
  input  S,
  output Y
);

  wire AND_1_out, AND_2_out, NOT_out;

  not NOT (NOT_out, B);
  and AND_1 (AND_1_out, B, S0);
  and AND_2 (AND_2_out, NOT_out, S);
  or OR (Y, AND_1_out, AND_2_out);

  // Notes on the sheet:
  //   Roll: 1607048
endmodule
