// Logisim project Half Adder.circ as structural Verilog: 2 circuits, main circuit main
module main (
  input  X,
  input  Y,
  output Sum,
  output Carry
);

  wire AND1_2_out, AND1_out, NOT1_out, NOT2_out;

  not NOT1 (NOT1_out, X);
  not NOT2 (NOT2_out, Y);
  and AND1 (AND1_out, NOT1_out, Y);
  and AND1_2 (AND1_2_out, X, NOT2_out);
  and AND3 (Carry, X, Y);
  or OR (Sum, AND1_out, AND1_2_out);

  // Notes on the sheet:
  //   HALF ADDER
endmodule

module HA_XOR (
  input  X,
  input  Y
);

  wire AND_out, XOR_out;

  xor XOR (XOR_out, X, Y);
  and AND (AND_out, X, Y);
  LED S (.in(XOR_out));
  LED C (.in(AND_out));

  // Notes on the sheet:
  //   Sum
  //   Carry
endmodule
