// Logisim project RTL 1607048.circ as structural Verilog: 2 circuits, main circuit main
module main (
  input  [3:0] INPUT,
  input  LOAD,
  input  LOAD_2,
  input  CLK,
  input  CLK_2,
  input  CLR,
  input  CLR_2,
  input  ENABLE,
  input  ENABLE_2,
  input  LOAD_3,
  input  LOAD_4,
  input  CLK_3,
  input  CLK_4,
  input  CLR_3,
  input  CLR_4,
  input  ENABLE_3,
  input  ENABLE_4,
  output [3:0] OUTPUT
);

  Register register_1 (
    .X3(OUTPUT[3]), .X2(OUTPUT[2]), .X1(OUTPUT[1]), .X0(OUTPUT[0]), .Y3(OUTPUT[3]), .Y2(OUTPUT[2]),
    .Y1(OUTPUT[1]), .Y0(OUTPUT[0]), .LOAD(LOAD), .CLK(CLK), .CLR(CLR_2), .ENABLE(ENABLE_2));
  Register register_2 (
    .X3(OUTPUT[3]), .X2(OUTPUT[2]), .X1(OUTPUT[1]), .X0(OUTPUT[0]), .Y3(OUTPUT[3]), .Y2(OUTPUT[2]),
    .Y1(OUTPUT[1]), .Y0(OUTPUT[0]), .LOAD(LOAD_3), .CLK(CLK_3), .CLR(CLR_4), .ENABLE(ENABLE_4));
  Register register_3 (
    .X3(OUTPUT[3]), .X2(OUTPUT[2]), .X1(OUTPUT[1]), .X0(OUTPUT[0]), .Y3(OUTPUT[3]), .Y2(OUTPUT[2]),
    .Y1(OUTPUT[1]), .Y0(OUTPUT[0]), .LOAD(LOAD_2), .CLK(CLK_2), .CLR(CLR), .ENABLE(ENABLE));
  Register register_4 (
    .X3(OUTPUT[3]), .X2(OUTPUT[2]), .X1(OUTPUT[1]), .X0(OUTPUT[0]), .Y3(OUTPUT[3]), .Y2(OUTPUT[2]),
    .Y1(OUTPUT[1]), .Y0(OUTPUT[0]), .LOAD(LOAD_4), .CLK(CLK_4), .CLR(CLR_3), .ENABLE(ENABLE_3));

  // Notes on the sheet:
  //   input=0100
  //   Roll: 1607048
endmodule

// A
module Register (
  input  X3,
  input  X2,
  input  X1,
  input  X0,
  input  LOAD,
  input  CLK,
  input  CLR,
  input  ENABLE,
  output Y3,
  output Y2,
  output Y1,
  output Y0
);

  wire and_1_out, and_2_out, and_3_out, and_4_out, and_5_out, and_6_out, and_7_out, and_8_out, d_ff_1_q,
       d_ff_2_q, d_ff_3_q, d_ff_4_q, not_1_out, or_1_out, or_2_out, or_3_out, or_4_out;

  and and_1 (and_1_out, X3, LOAD);
  and and_2 (and_2_out, d_ff_1_q, not_1_out);
  or or_1 (or_1_out, and_2_out, and_1_out);
  D_Flip_Flop d_ff_1 (.clk(CLK), .D(or_1_out), .Q(d_ff_1_q), .reset(CLR));  // open: Qn, preset, en
  assign Y3 = ENABLE ? d_ff_1_q : 1'bz;  // Controlled_Buffer controlled_buffer_1
  and and_3 (and_3_out, d_ff_2_q, not_1_out);
  or or_2 (or_2_out, and_3_out, and_4_out);
  and and_4 (and_4_out, X2, LOAD);
  D_Flip_Flop d_ff_2 (.clk(CLK), .D(or_2_out), .Q(d_ff_2_q), .reset(CLR));  // open: Qn, preset, en
  assign Y2 = ENABLE ? d_ff_2_q : 1'bz;  // Controlled_Buffer controlled_buffer_2
  buf and_5 (and_5_out, d_ff_3_q);  // AND_Gate
  or or_3 (or_3_out, and_5_out, and_6_out);
  and and_6 (and_6_out, X1, LOAD);
  D_Flip_Flop d_ff_3 (.clk(CLK), .D(or_3_out), .Q(d_ff_3_q), .reset(CLR));  // open: Qn, preset, en
  and and_7 (and_7_out, d_ff_4_q, not_1_out);
  assign Y1 = ENABLE ? d_ff_3_q : 1'bz;  // Controlled_Buffer controlled_buffer_3
  not not_1 (not_1_out, LOAD);
  and and_8 (and_8_out, X0, LOAD);
  or or_4 (or_4_out, and_7_out, and_8_out);
  D_Flip_Flop d_ff_4 (.clk(CLK), .D(or_4_out), .Q(d_ff_4_q), .reset(CLR));  // open: Qn, preset, en
  assign Y0 = ENABLE ? d_ff_4_q : 1'bz;  // Controlled_Buffer controlled_buffer_4

  // Notes on the sheet:
  //   Faisal Ahmed
  //   Roll: 1607048
endmodule
